# Fritzing sketch arm electronics (saved by Fritzing 0.9.9b)
breadboards: 1

parts:
  U1 = ESP32S-HiLetgo [part_number=ESP32S-HiLetgo]
  L1 = Solenoid
  Power_plug1 = Power plug
  J2 = Basic Servo
  J3 = Basic Servo
  J4 = Basic Servo
  J5 = Basic Servo
  J6 = Basic Servo
  Q5 = NPN-Transistor [package="TO92 [THT]"]
  Q3 = NPN-Transistor [package="TO92 [THT]"]
  Q4 = NPN-Transistor [package="TO92 [THT]"]
  Q1 = NPN-Transistor [package="TO92 [THT]"]
  Q2 = NPN-Transistor [package="TO92 [THT]"]
  Q6 = NPN-Transistor [package="TO92 [THT]"]
  S1 = Round Pushbutton
  Part1 = OMRON PCB Power Relay – G5LE [part_number="G5LE-1\r\n" package=THT]

nets:
  N1: U1.GPIO33, Q3.B
  N2: U1.GPIO25, Q4.B
  N3: U1.GPIO26, Q5.B
  GND: U1.GND, L1.pin1, Power_plug1.GND, J2.gnd, J3.gnd, J4.gnd, J5.gnd, J6.gnd, Part1.COIL1
  N4: U1.GPIO11, Part1.COIL2
  N5: U1.GPIO16, S1.leg1
  N6: U1.GPIO5, Q6.B
  N7: U1.GPIO18, Q2.B
  N8: U1.GPIO19, Q1.B
  N9: L1.pin2, Q6.E
  N10: Power_plug1.VCC, Part1.B
  VCC: J2.vcc, J3.vcc, J4.vcc, J5.vcc, J6.vcc, Q5.C, Q3.C, Q4.C, Q1.C, Q2.C, Q6.C, Part1.C
  N11: J2.pulse, Q1.E
  N12: J3.pulse, Q2.E
  N13: J4.pulse, Q3.E
  N14: J5.pulse, Q4.E
  N15: J6.pulse, Q5.E
  N16: S1.leg0, Part1.A

notes:
  5V power line
  3.3V power line

custom parts:
  ESP32S-HiLetgo: HiLetgo ESP-WROOM-32 ESP32 ESP-32S Development Board 2.4GHz Dual-Mode WiFi + Bluetooth Dual Cores Microcontroller The ESP32 integrated with Antenna switches, RF Balun, power amplifiers, low-noise amplifiers, filters, and management modules, and the entire solution occupies the least area of PCB. 2.4 GHz Wi-Fi plus Bluetooth dual-mode chip, with TSMC Ultra-low power consumption 40nm technology,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
